// Digital circuit sram.dig as structural Verilog
// 16-bit static RAM.
// Below the memory matrix, the write logic is found 
// once for each column in the memory matrix.
// 16-Bit Statisches RAM.
// {{de Unter der Speichermatrix findet sich die 
// Schreiblogik jeweils einmal für jede Spalte in der 
// Speichermatrix.}}
module sram (
  input  D_In,
  input  R0,
  input  R1,
  input  C0,
  input  C1,
  input  WE,
  output D_Out
);

  wire decoder_1_out_0, decoder_1_out_1, decoder_1_out_2, decoder_1_out_3, demultiplexer_1_out_0,
       demultiplexer_1_out_1, demultiplexer_1_out_2, demultiplexer_1_out_3, driver_1_out, driver_5_out,
       nfet_1_s, nfet_2_s, nfet_3_s, nfet_4_s, nfet_5_s, nfet_6_s, nfet_7_s, nfet_8_s, nfet_9_s, nfet_10_s,
       nfet_11_s, nfet_13_s, nfet_15_s, nfet_17_d, nfet_17_s, nfet_18_s, nfet_19_s, nfet_20_s, nfet_21_s,
       nfet_22_s, nfet_23_s, nfet_24_s, nfet_25_s, nfet_26_s, nfet_27_s, nfet_28_s, nfet_29_s, nfet_33_s,
       nfet_34_s, nfet_35_s, nfet_36_s, nfet_37_s, nfet_38_s, nfet_39_s, nfet_40_s, nfet_41_s, nfet_42_s,
       nfet_43_s, nfet_45_s, nfet_47_s, nfet_49_d, nfet_49_s, nfet_50_s, nfet_51_s, nfet_52_s, nfet_53_s,
       nfet_54_s, nfet_55_s, nfet_56_s, nfet_57_s, nfet_58_s, nfet_59_s, nfet_60_s, nfet_61_s, not_1_out,
       pfet_1_d, pfet_2_d, pfet_3_d, pfet_4_d, pfet_9_d, pfet_10_d, pfet_11_d, pfet_12_d, pfet_17_d,
       pfet_18_d, pfet_19_d, pfet_20_d, pfet_25_d, pfet_26_d, pfet_27_d, pfet_28_d, pullup_1_out,
       pullup_2_out, pullup_3_out, pullup_4_out, pullup_5_out, pullup_6_out, pullup_7_out, pullup_8_out,
       pullup_9_out, pullup_10_out, pullup_11_out, pullup_12_out, pullup_13_out, pullup_14_out,
       pullup_15_out, pullup_16_out, pullup_17_out, pullup_18_out, pullup_19_out, pullup_20_out,
       pullup_21_out, pullup_22_out, pullup_23_out, pullup_24_out, pullup_25_out, pullup_26_out,
       pullup_27_out, pullup_28_out, pullup_29_out, pullup_30_out, pullup_31_out, pullup_32_out;

  Decoder #(.Selector_Bits(2)) decoder_1 (
    .sel({R1, R0}), .out_0(decoder_1_out_0), .out_1(decoder_1_out_1), .out_2(decoder_1_out_2),
    .out_3(decoder_1_out_3));
  Demultiplexer #(.Selector_Bits(2)) demultiplexer_1 (
    .sel({C1, C0}), .in(WE), .out_0(demultiplexer_1_out_0), .out_1(demultiplexer_1_out_1),
    .out_2(demultiplexer_1_out_2), .out_3(demultiplexer_1_out_3));
  assign driver_1_out = demultiplexer_1_out_0 ? not_1_out : 1'bz;  // Driver driver_1
  not not_1 (not_1_out, D_In);
  NFET nfet_1 (.G(decoder_1_out_0), .D(driver_1_out), .S(nfet_1_s));
  NFET nfet_2 (.G(decoder_1_out_1), .D(driver_1_out), .S(nfet_2_s));
  NFET nfet_3 (.G(decoder_1_out_2), .D(driver_1_out), .S(nfet_3_s));
  NFET nfet_4 (.G(decoder_1_out_3), .D(driver_1_out), .S(nfet_4_s));
  PullUp pullup_1 (.out(pullup_1_out));
  LED led_1 (.in(pfet_1_d));
  PFET pfet_1 (.G(nfet_1_s), .S(pullup_1_out), .D(pfet_1_d));
  NFET nfet_5 (.G(nfet_1_s), .D(pfet_1_d), .S(nfet_5_s));
  PullDown pulldown_1 (.out(nfet_5_s));
  PullUp pullup_2 (.out(pullup_2_out));
  LED led_2 (.in(pfet_2_d));
  PFET pfet_2 (.G(nfet_2_s), .S(pullup_2_out), .D(pfet_2_d));
  NFET nfet_6 (.G(nfet_2_s), .D(pfet_2_d), .S(nfet_6_s));
  PullDown pulldown_2 (.out(nfet_6_s));
  PullUp pullup_3 (.out(pullup_3_out));
  LED led_3 (.in(pfet_3_d));
  PFET pfet_3 (.G(nfet_3_s), .S(pullup_3_out), .D(pfet_3_d));
  NFET nfet_7 (.G(nfet_3_s), .D(pfet_3_d), .S(nfet_7_s));
  PullDown pulldown_3 (.out(nfet_7_s));
  PullUp pullup_4 (.out(pullup_4_out));
  LED led_4 (.in(pfet_4_d));
  PFET pfet_4 (.G(nfet_4_s), .S(pullup_4_out), .D(pfet_4_d));
  NFET nfet_8 (.G(nfet_4_s), .D(pfet_4_d), .S(nfet_8_s));
  PullDown pulldown_4 (.out(nfet_8_s));
  PullUp pullup_5 (.out(pullup_5_out));
  PFET pfet_5 (.G(pfet_1_d), .S(pullup_5_out), .D(nfet_1_s));
  NFET nfet_9 (.G(pfet_1_d), .D(nfet_1_s), .S(nfet_9_s));
  NFET nfet_10 (.G(decoder_1_out_0), .D(pfet_1_d), .S(nfet_10_s));
  PullDown pulldown_5 (.out(nfet_9_s));
  PullUp pullup_6 (.out(pullup_6_out));
  PFET pfet_6 (.G(pfet_2_d), .S(pullup_6_out), .D(nfet_2_s));
  NFET nfet_11 (.G(pfet_2_d), .D(nfet_2_s), .S(nfet_11_s));
  NFET nfet_12 (.G(decoder_1_out_1), .D(pfet_2_d), .S(nfet_10_s));
  PullDown pulldown_6 (.out(nfet_11_s));
  PullUp pullup_7 (.out(pullup_7_out));
  PFET pfet_7 (.G(pfet_3_d), .S(pullup_7_out), .D(nfet_3_s));
  NFET nfet_13 (.G(pfet_3_d), .D(nfet_3_s), .S(nfet_13_s));
  NFET nfet_14 (.G(decoder_1_out_2), .D(pfet_3_d), .S(nfet_10_s));
  PullDown pulldown_7 (.out(nfet_13_s));
  PullUp pullup_8 (.out(pullup_8_out));
  PFET pfet_8 (.G(pfet_4_d), .S(pullup_8_out), .D(nfet_4_s));
  NFET nfet_15 (.G(pfet_4_d), .D(nfet_4_s), .S(nfet_15_s));
  NFET nfet_16 (.G(decoder_1_out_3), .D(pfet_4_d), .S(nfet_10_s));
  PullDown pulldown_8 (.out(nfet_15_s));
  assign nfet_10_s = demultiplexer_1_out_0 ? D_In : 1'bz;  // Driver driver_2
  NFET nfet_17 (.G(decoder_1_out_0), .D(nfet_17_d), .S(nfet_17_s));
  NFET nfet_18 (.G(decoder_1_out_1), .D(nfet_17_d), .S(nfet_18_s));
  NFET nfet_19 (.G(decoder_1_out_2), .D(nfet_17_d), .S(nfet_19_s));
  NFET nfet_20 (.G(decoder_1_out_3), .D(nfet_17_d), .S(nfet_20_s));
  assign nfet_17_d = demultiplexer_1_out_1 ? not_1_out : 1'bz;  // Driver driver_3
  PullUp pullup_9 (.out(pullup_9_out));
  PFET pfet_9 (.G(nfet_17_s), .S(pullup_9_out), .D(pfet_9_d));
  NFET nfet_21 (.G(nfet_17_s), .D(pfet_9_d), .S(nfet_21_s));
  PullDown pulldown_9 (.out(nfet_21_s));
  PullUp pullup_10 (.out(pullup_10_out));
  PFET pfet_10 (.G(nfet_18_s), .S(pullup_10_out), .D(pfet_10_d));
  NFET nfet_22 (.G(nfet_18_s), .D(pfet_10_d), .S(nfet_22_s));
  PullDown pulldown_10 (.out(nfet_22_s));
  PullUp pullup_11 (.out(pullup_11_out));
  PFET pfet_11 (.G(nfet_19_s), .S(pullup_11_out), .D(pfet_11_d));
  NFET nfet_23 (.G(nfet_19_s), .D(pfet_11_d), .S(nfet_23_s));
  PullDown pulldown_11 (.out(nfet_23_s));
  PullUp pullup_12 (.out(pullup_12_out));
  PFET pfet_12 (.G(nfet_20_s), .S(pullup_12_out), .D(pfet_12_d));
  NFET nfet_24 (.G(nfet_20_s), .D(pfet_12_d), .S(nfet_24_s));
  PullDown pulldown_12 (.out(nfet_24_s));
  PullUp pullup_13 (.out(pullup_13_out));
  LED led_5 (.in(pfet_9_d));
  PFET pfet_13 (.G(pfet_9_d), .S(pullup_13_out), .D(nfet_17_s));
  NFET nfet_25 (.G(pfet_9_d), .D(nfet_17_s), .S(nfet_25_s));
  PullDown pulldown_13 (.out(nfet_25_s));
  PullUp pullup_14 (.out(pullup_14_out));
  LED led_6 (.in(pfet_10_d));
  PFET pfet_14 (.G(pfet_10_d), .S(pullup_14_out), .D(nfet_18_s));
  NFET nfet_26 (.G(pfet_10_d), .D(nfet_18_s), .S(nfet_26_s));
  PullDown pulldown_14 (.out(nfet_26_s));
  PullUp pullup_15 (.out(pullup_15_out));
  LED led_7 (.in(pfet_11_d));
  PFET pfet_15 (.G(pfet_11_d), .S(pullup_15_out), .D(nfet_19_s));
  NFET nfet_27 (.G(pfet_11_d), .D(nfet_19_s), .S(nfet_27_s));
  PullDown pulldown_15 (.out(nfet_27_s));
  PullUp pullup_16 (.out(pullup_16_out));
  LED led_8 (.in(pfet_12_d));
  PFET pfet_16 (.G(pfet_12_d), .S(pullup_16_out), .D(nfet_20_s));
  NFET nfet_28 (.G(pfet_12_d), .D(nfet_20_s), .S(nfet_28_s));
  PullDown pulldown_16 (.out(nfet_28_s));
  NFET nfet_29 (.G(decoder_1_out_0), .D(pfet_9_d), .S(nfet_29_s));
  NFET nfet_30 (.G(decoder_1_out_1), .D(pfet_10_d), .S(nfet_29_s));
  NFET nfet_31 (.G(decoder_1_out_2), .D(pfet_11_d), .S(nfet_29_s));
  NFET nfet_32 (.G(decoder_1_out_3), .D(pfet_12_d), .S(nfet_29_s));
  assign nfet_29_s = demultiplexer_1_out_1 ? D_In : 1'bz;  // Driver driver_4
  assign driver_5_out = demultiplexer_1_out_2 ? not_1_out : 1'bz;  // Driver driver_5
  NFET nfet_33 (.G(decoder_1_out_0), .D(driver_5_out), .S(nfet_33_s));
  NFET nfet_34 (.G(decoder_1_out_1), .D(driver_5_out), .S(nfet_34_s));
  NFET nfet_35 (.G(decoder_1_out_2), .D(driver_5_out), .S(nfet_35_s));
  NFET nfet_36 (.G(decoder_1_out_3), .D(driver_5_out), .S(nfet_36_s));
  PullUp pullup_17 (.out(pullup_17_out));
  LED led_9 (.in(pfet_17_d));
  PFET pfet_17 (.G(nfet_33_s), .S(pullup_17_out), .D(pfet_17_d));
  NFET nfet_37 (.G(nfet_33_s), .D(pfet_17_d), .S(nfet_37_s));
  PullDown pulldown_17 (.out(nfet_37_s));
  PullUp pullup_18 (.out(pullup_18_out));
  LED led_10 (.in(pfet_18_d));
  PFET pfet_18 (.G(nfet_34_s), .S(pullup_18_out), .D(pfet_18_d));
  NFET nfet_38 (.G(nfet_34_s), .D(pfet_18_d), .S(nfet_38_s));
  PullDown pulldown_18 (.out(nfet_38_s));
  PullUp pullup_19 (.out(pullup_19_out));
  LED led_11 (.in(pfet_19_d));
  PFET pfet_19 (.G(nfet_35_s), .S(pullup_19_out), .D(pfet_19_d));
  NFET nfet_39 (.G(nfet_35_s), .D(pfet_19_d), .S(nfet_39_s));
  PullDown pulldown_19 (.out(nfet_39_s));
  PullUp pullup_20 (.out(pullup_20_out));
  LED led_12 (.in(pfet_20_d));
  PFET pfet_20 (.G(nfet_36_s), .S(pullup_20_out), .D(pfet_20_d));
  NFET nfet_40 (.G(nfet_36_s), .D(pfet_20_d), .S(nfet_40_s));
  PullDown pulldown_20 (.out(nfet_40_s));
  PullUp pullup_21 (.out(pullup_21_out));
  PFET pfet_21 (.G(pfet_17_d), .S(pullup_21_out), .D(nfet_33_s));
  NFET nfet_41 (.G(pfet_17_d), .D(nfet_33_s), .S(nfet_41_s));
  NFET nfet_42 (.G(decoder_1_out_0), .D(pfet_17_d), .S(nfet_42_s));
  PullDown pulldown_21 (.out(nfet_41_s));
  PullUp pullup_22 (.out(pullup_22_out));
  PFET pfet_22 (.G(pfet_18_d), .S(pullup_22_out), .D(nfet_34_s));
  NFET nfet_43 (.G(pfet_18_d), .D(nfet_34_s), .S(nfet_43_s));
  NFET nfet_44 (.G(decoder_1_out_1), .D(pfet_18_d), .S(nfet_42_s));
  PullDown pulldown_22 (.out(nfet_43_s));
  PullUp pullup_23 (.out(pullup_23_out));
  PFET pfet_23 (.G(pfet_19_d), .S(pullup_23_out), .D(nfet_35_s));
  NFET nfet_45 (.G(pfet_19_d), .D(nfet_35_s), .S(nfet_45_s));
  NFET nfet_46 (.G(decoder_1_out_2), .D(pfet_19_d), .S(nfet_42_s));
  PullDown pulldown_23 (.out(nfet_45_s));
  PullUp pullup_24 (.out(pullup_24_out));
  PFET pfet_24 (.G(pfet_20_d), .S(pullup_24_out), .D(nfet_36_s));
  NFET nfet_47 (.G(pfet_20_d), .D(nfet_36_s), .S(nfet_47_s));
  NFET nfet_48 (.G(decoder_1_out_3), .D(pfet_20_d), .S(nfet_42_s));
  PullDown pulldown_24 (.out(nfet_47_s));
  assign nfet_42_s = demultiplexer_1_out_2 ? D_In : 1'bz;  // Driver driver_6
  NFET nfet_49 (.G(decoder_1_out_0), .D(nfet_49_d), .S(nfet_49_s));
  NFET nfet_50 (.G(decoder_1_out_1), .D(nfet_49_d), .S(nfet_50_s));
  NFET nfet_51 (.G(decoder_1_out_2), .D(nfet_49_d), .S(nfet_51_s));
  NFET nfet_52 (.G(decoder_1_out_3), .D(nfet_49_d), .S(nfet_52_s));
  assign nfet_49_d = demultiplexer_1_out_3 ? not_1_out : 1'bz;  // Driver driver_7
  PullUp pullup_25 (.out(pullup_25_out));
  PFET pfet_25 (.G(nfet_49_s), .S(pullup_25_out), .D(pfet_25_d));
  NFET nfet_53 (.G(nfet_49_s), .D(pfet_25_d), .S(nfet_53_s));
  PullDown pulldown_25 (.out(nfet_53_s));
  PullUp pullup_26 (.out(pullup_26_out));
  PFET pfet_26 (.G(nfet_50_s), .S(pullup_26_out), .D(pfet_26_d));
  NFET nfet_54 (.G(nfet_50_s), .D(pfet_26_d), .S(nfet_54_s));
  PullDown pulldown_26 (.out(nfet_54_s));
  PullUp pullup_27 (.out(pullup_27_out));
  PFET pfet_27 (.G(nfet_51_s), .S(pullup_27_out), .D(pfet_27_d));
  NFET nfet_55 (.G(nfet_51_s), .D(pfet_27_d), .S(nfet_55_s));
  PullDown pulldown_27 (.out(nfet_55_s));
  PullUp pullup_28 (.out(pullup_28_out));
  PFET pfet_28 (.G(nfet_52_s), .S(pullup_28_out), .D(pfet_28_d));
  NFET nfet_56 (.G(nfet_52_s), .D(pfet_28_d), .S(nfet_56_s));
  PullDown pulldown_28 (.out(nfet_56_s));
  PullUp pullup_29 (.out(pullup_29_out));
  LED led_13 (.in(pfet_25_d));
  PFET pfet_29 (.G(pfet_25_d), .S(pullup_29_out), .D(nfet_49_s));
  NFET nfet_57 (.G(pfet_25_d), .D(nfet_49_s), .S(nfet_57_s));
  PullDown pulldown_29 (.out(nfet_57_s));
  PullUp pullup_30 (.out(pullup_30_out));
  LED led_14 (.in(pfet_26_d));
  PFET pfet_30 (.G(pfet_26_d), .S(pullup_30_out), .D(nfet_50_s));
  NFET nfet_58 (.G(pfet_26_d), .D(nfet_50_s), .S(nfet_58_s));
  PullDown pulldown_30 (.out(nfet_58_s));
  PullUp pullup_31 (.out(pullup_31_out));
  LED led_15 (.in(pfet_27_d));
  PFET pfet_31 (.G(pfet_27_d), .S(pullup_31_out), .D(nfet_51_s));
  NFET nfet_59 (.G(pfet_27_d), .D(nfet_51_s), .S(nfet_59_s));
  PullDown pulldown_31 (.out(nfet_59_s));
  PullUp pullup_32 (.out(pullup_32_out));
  LED led_16 (.in(pfet_28_d));
  PFET pfet_32 (.G(pfet_28_d), .S(pullup_32_out), .D(nfet_52_s));
  NFET nfet_60 (.G(pfet_28_d), .D(nfet_52_s), .S(nfet_60_s));
  PullDown pulldown_32 (.out(nfet_60_s));
  NFET nfet_61 (.G(decoder_1_out_0), .D(pfet_25_d), .S(nfet_61_s));
  NFET nfet_62 (.G(decoder_1_out_1), .D(pfet_26_d), .S(nfet_61_s));
  NFET nfet_63 (.G(decoder_1_out_2), .D(pfet_27_d), .S(nfet_61_s));
  NFET nfet_64 (.G(decoder_1_out_3), .D(pfet_28_d), .S(nfet_61_s));
  assign nfet_61_s = demultiplexer_1_out_3 ? D_In : 1'bz;  // Driver driver_8
  Multiplexer #(.Selector_Bits(2)) multiplexer_1 (
    .sel({C1, C0}), .in_0(nfet_10_s), .in_1(nfet_29_s), .in_2(nfet_42_s), .in_3(nfet_61_s), .out(D_Out));

  // Notes on the sheet:
  //   D_In: Data input to write the bits.
  //   {{de Dateneingang zum Schreiben der Bits.}}
  //   R0: Row input 0
  //   {{de Zeilenleitung Bit 0}}
  //   R1: Row input 1
  //   {{de Zeilenleitung Bit 1}}
  //   D_Out: Data output to read the bits.
  //   {{de Datenausgang zum Lesen der Bits.}}
  //   C0: column input 0
  //   {{de Spaltenleitung Bit 0}}
  //   C1: column input 0
  //   {{de Spaltenleitung Bit 1}}
  //   WE: Write-Enable.
  //   If this input goes to one, the data input is 
  //   stored in the memory matrix.
  //   {{de Schreibfreigabe
  //   Geht diese Leitung auf Eins, wird der Dateneingang
  //   in der Speichermatrix gespeichert.}}
  //   16-Bit SRAM {{de 16-Bit SRAM}}
endmodule

/* Test case:
C0 C1 R0 R1 WE D_In D_Out

# write all cells to one
loop(n,16)
bits(4,n)    0  1    0
bits(4,n)    1  1    1
bits(4,n)    0  1    1
end loop

# check all cells are one
repeat(16) bits(4,n)    0  x    1

# write all cells to zero
loop(n,16)
bits(4,n)    0  0    1
bits(4,n)    1  0    0
bits(4,n)    0  0    0
end loop

# check all cells are zero
repeat(16) bits(4,n)    0  x    0

#write cell 00 to 1

0  0  0  0  0  0    0
0  0  0  0  1  1    1
0  0  0  0  0  1    1
0  0  0  0  0  0    1

# cell 11 is still zero

0  1  0  1  0  0    0

# cell 00 is still 1

0  0  0  0  0  0    1
*/
