// Digital circuit Bus.dig as structural Verilog
module Bus (
  input  clk
);

  wire decoder_1_out_0, decoder_1_out_1, decoder_1_out_2, decoder_1_out_3;
  wire [4:0] Address_out;
  wire [7:0] rom_1_d;

  Counter #(.Bits(5)) Address (.en(clk), .C(1'b0), .out(Address_out));  // open: clr, ovf
  Decoder #(.Selector_Bits(2)) decoder_1 (
    .sel(Address_out[4:3]), .out_0(decoder_1_out_0), .out_1(decoder_1_out_1), .out_2(decoder_1_out_2),
    .out_3(decoder_1_out_3));
  ROM #(.Bits(8), .Addr_Bits(3)) rom_1 (.A(Address_out[2:0]), .sel(decoder_1_out_0), .D(rom_1_d));
  ROM #(.Bits(8), .Addr_Bits(3)) rom_2 (.A(Address_out[2:0]), .sel(decoder_1_out_1), .D(rom_1_d));
  ROM #(.Bits(8), .Addr_Bits(3)) rom_3 (.A(Address_out[2:0]), .sel(decoder_1_out_2), .D(rom_1_d));
  ROM #(.Bits(8), .Addr_Bits(3)) rom_4 (.A(Address_out[2:0]), .sel(decoder_1_out_3), .D(rom_1_d));
  // Probe D on rom_1_d

  // Notes on the sheet:
  //   clk: Hz: 2
  //   contents of rom_1 (hex, n*v repeats v):
  //   8
  //   68
  //   105
  //   101
  //   115
  //   32
  //   105
  //   115
  //   116
  //   8
  //   contents of rom_2 (hex, n*v repeats v):
  //   8
  //   32
  //   101
  //   105
  //   110
  //   32
  //   108
  //   97
  //   110
  //   8
  //   contents of rom_3 (hex, n*v repeats v):
  //   8
  //   103
  //   101
  //   114
  //   32
  //   84
  //   101
  //   115
  //   116
  //   8
  //   contents of rom_4 (hex, n*v repeats v):
  //   8
  //   116
  //   101
  //   120
  //   116
  //   46
  //   32
  //   32
  //   32
  //   8
endmodule
