// Digital circuit Comp7485.dig as structural Verilog
module Comp7485 (
  input  P_0,
  input  P_1,
  input  P_2,
  input  P_3,
  input  P_lt_Q_i,
  input  P_eq_Q_i,
  input  P_gt_Q_i,
  input  Q_0,
  input  Q_1,
  input  Q_2,
  input  Q_3,
  output P_lt_Q,
  output P_eq_Q,
  output P_gt_Q
);

  wire comprc_1_p_eq_q, comprc_1_p_gt_q, comprc_1_p_lt_q;

  CompRC comprc_1 (
    .P_3(P_3), .P_2(P_2), .P_1(P_1), .P_0(P_0), .Q_3(Q_3), .Q_2(Q_2), .Q_1(Q_1), .Q_0(Q_0),
    .P_lt_Q(comprc_1_p_lt_q), .P_eq_Q(comprc_1_p_eq_q), .P_gt_Q(comprc_1_p_gt_q));
  Multiplexer multiplexer_1 (.sel(comprc_1_p_eq_q), .in_0(comprc_1_p_lt_q), .in_1(P_lt_Q_i), .out(P_lt_Q));
  Multiplexer multiplexer_2 (.sel(comprc_1_p_eq_q), .in_0(comprc_1_p_eq_q), .in_1(P_eq_Q_i), .out(P_eq_Q));
  Multiplexer multiplexer_3 (.sel(comprc_1_p_eq_q), .in_0(comprc_1_p_gt_q), .in_1(P_gt_Q_i), .out(P_gt_Q));
endmodule
