// Digital circuit barrelShifter.dig as structural Verilog
// Barrel-Shifter with selectable bit width.
// {{de Barrel-Shifter mit wählbarer Bitbreite.}}
module barrelShifter (
  input  [15:0] D_in,
  input  [3:0] sh,
  output [15:0] D
);

  shift_inc #(.generic("if (isPresent(args)) { if (args.dir=\"right\") { export circuit:=\"shift-fixed-right-inc.dig\"; } else { if (args.dir=\"arith\") { export circuit:=\"shift-fixed-arith-right-inc.dig\"; } else { if (args.dir=\"left\") { export circuit:=\"shift-fixed-left-inc.dig\"; } else { panic(\"only \\\"left\\\", \\\"right\\\" or \\\"arith\\\" is allowed as direction, not \\\"\"+args.dir+\"\\\"!\"); } } } export shiftBits:=bitsNeededFor(args.d")) shift_inc_1 (
    .D_in(D_in), .sh(sh), .D(D));
endmodule
