// Digital circuit Interrupt.dig as structural Verilog
// Einfacher Interrupt-Controller.
// Wird ein Interrupt ausgelöst, wird der Controller
// gesperrt: Es können keine weiteren Interrupts
// ausgelöst werden. Erst der Eingang reti gibt den 
// Interrupt-Controller wieder frei.
module Interrupt (
  input  C,
  input  [15:0] Next,
  input  rel,
  input  imm,
  input  abs,
  input  reti,
  input  intr,
  output [15:0] retAddr,
  output iEn
);

  wire and_1_out, intLock_nq, not_1_out, not_2_out, not_3_out, rising_1_p3;

  // Rising rising_1: pin names not known; wires that end beside it: iEn, intr, rising_1_p3
  not not_1 (not_1_out, imm);
  not not_2 (not_2_out, rel);
  not not_3 (not_3_out, abs);
  JK_FF intLock (.J(and_1_out), .C(C), .K(reti), .nQ(intLock_nq));  // open: Q
  and and_1 (and_1_out, intLock_nq, rising_1_p3, not_1_out, not_2_out, not_3_out);
  Register #(.Bits(16)) u_retAddr (.D(Next), .C(C), .en(and_1_out), .Q(retAddr));
  D_FF u_iEn (.D(and_1_out), .C(C), .Q(iEn));  // open: nQ

  // Notes on the sheet:
  //   retAddr: Return Address
  //   C: Takt
  //   Next: Der nächste Befehl, also die Rücksprungadresse.
  //   iEn: Interrupt-Freigabe für PC
  //   rel: relativer Sprung: 
  //   Wenn gesetzt, wird Interrupt verhindert.
  //   imm: Immediate Register:
  //   Wenn gesetzt, wird Interrupt verhindert.
  //   abs: Absoluter Sprung:
  //   Wenn gesetzt, wird Interrupt verhindert.
  //   reti: return from interrupt. Über dieses Signal werden
  //   die Interrupts wieder freigegeben.
  //   intr: Interrupt Anforderung
endmodule
