// Digital circuit SignExt.dig as structural Verilog
// Extrahiert kleine Konstanten aus dem Befehlswort.
// Es können zwei 5-Bit Konstanten (Die 4 Bits eines 
// Registers zusammen mit Bit 8 des Befehlswortes)
// und eine 9-Bit Konstante (Die 8 Bits beider Register
// zusammen mit Bit 8 des Befehlswortes)
module SignExt (
  input  [15:0] inst,
  output [15:0] _5S,
  output [15:0] _9SD,
  output [15:0] _5D
);

  PullDown #(.Bits(16)) pulldown_1 (.out(inst));

  assign _5D = {{11{1'b0}}, inst[8:4]};
  assign _5S = {{11{1'b0}}, inst[8], inst[3:0]};
  assign _9SD = {{8{inst[8]}}, inst[7:0]};

  // Notes on the sheet:
  //   inst: Das Befehlswort
  //   _5S: Die fünf Bit aus Rs und Bit 8
  //   _9SD: Die neun Bit aus Rs,Rd und Bit 8
  //   _5D: Die fünf Bit aus Rd und Bit 8
endmodule
