// Digital circuit multip_D_working.dig as structural Verilog
module multip_D_working (
  input  D,
  input  C,
  output Q
);

  wire d_ms_1_p3, d_ms_2_p3;

  // D_MS d_ms_1: pin names not known; wires that end beside it: D, C, d_ms_1_p3
  // D_MS d_ms_2: pin names not known; wires that end beside it: d_ms_1_p3, C, d_ms_2_p3
  // D_MS d_ms_3: pin names not known; wires that end beside it: d_ms_2_p3, C, Q
endmodule
