// Digital circuit ArduinoUno.dig as structural Verilog
module ArduinoUno (
  input  R,
  input  C,
  output [7:0] TxD,
  output TxC,
  output D0,
  output D1,
  output D2,
  output D3,
  output D4,
  output D5,
  output D6,
  output D7,
  output D8,
  output D9,
  output D10,
  output D11,
  output D12,
  output D13,
  output D14,
  output D15,
  output D16,
  output D17,
  output D18,
  output D19
);

  // Simavr #(.generic("this.simavrFirmwareFilePath = args.firmwareFilePath;")) simavr_1: pin names not known; wires that end beside it: R, C, TxC, TxD, {2'b00, D13, D12, D11, D10, D9, D8}, {1'b1, D19, D18, D17, D16, D15, D14}, {D7, D6, D5, D4, D3, D2, D1, D0}

  // Notes on the sheet:
  //   R: Reset
  //   TxD: TX Data (8-bit)
  //   TxC: TX Clock
endmodule

/* Code that sets the parameters or builds the circuit:
firmwareFilePath := "src/test/resources/simavr/test-firmware/firmware.elf";
*/
