// Digital circuit ArduinoUnoExample.dig as structural Verilog
module ArduinoUnoExample (
  input  clk,
  output [7:0] out_1,
  output out_2,
  output out_3,
  output out_4,
  output out_5,
  output out_6,
  output out_7,
  output out_8,
  output out_9,
  output out_10,
  output out_11,
  output out_12,
  output out_13,
  output out_14,
  output out_15,
  output out_16,
  output out_17,
  output out_18,
  output out_19,
  output out_20
);

  wire reset_1_out;

  Reset #(.invertOutput("false")) reset_1 (.out(reset_1_out));
  ArduinoUno #(.generic("firmwareFilePath := ;")) arduinouno_1 (
    .R(reset_1_out), .C(clk), .TxD(out_1), .TxC(out_2), .D0(out_3), .D1(out_4), .D2(out_5), .D3(out_6),
    .D4(out_7), .D5(out_8), .D6(out_9), .D7(out_10), .D8(out_11), .D9(out_12), .D10(out_13), .D11(out_14),
    .D12(out_15), .D13(out_16), .D14(out_17), .D15(out_18), .D16(out_19), .D17(out_20));  // open: D18, D19
  // Pins of 1 and 8 bits meet at out_1
endmodule
